# Fritzing sketch robbo (saved by Fritzing 0.7.4b)
breadboards: 1

parts:
  FEZ_Panda_II1 = FEZ Panda II
  VCC1 = Battery block 9V
  Part1 = Dual Motor Driver TB6612FNG
  M1 = DC Motor
  M2 = DC Motor
  Part2 = Triple Axis Accelerometer Breakout - ADXL345
  VCC2 = 4 x AAA Battery Mount
  Part3 = MaxBotix LZ-EV0

nets:
  N1: FEZ_Panda_II1.A5, Part3.AN
  GND: FEZ_Panda_II1.GND#35, Part2.GND, Part2.SDO, Part3.GND
  N2: FEZ_Panda_II1.GND#36, VCC1.-
  N3: FEZ_Panda_II1.VIN, VCC1.+
  3V3: FEZ_Panda_II1.3V3, Part2.VCC, Part2.CS
  5V: FEZ_Panda_II1.5V, Part1.VCC, Part3.+5
  N4: FEZ_Panda_II1.Di2, Part2.SDA
  N5: FEZ_Panda_II1.Di3, Part2.SCL
  N6: FEZ_Panda_II1.Di4, Part1.BIN2
  N7: FEZ_Panda_II1.Di5, Part1.PWMB
  N8: FEZ_Panda_II1.Di6, Part1.BIN1
  N9: FEZ_Panda_II1.Di7, Part1.STBY
  N10: FEZ_Panda_II1.Di8, Part1.AIN1
  N11: FEZ_Panda_II1.Di9, Part1.AIN2
  N12: FEZ_Panda_II1.Di10, Part1.PWMA
  N13: FEZ_Panda_II1.Di11, Part3.RX
  N14: Part1.VM, VCC2.+
  N15: Part1.GND, VCC2.-
  N16: Part1.A01, M1.pin_1
  N17: Part1.A02, M1.pin_2
  N18: Part1.B02, M2.pin_2
  N19: Part1.B01, M2.pin_1

custom parts:
  FEZ Panda II: FEZ Panda II is a tiny open-source board running Microsoft .NET Micro Framework.
